# Fritzing sketch stimsync_pcb (saved by Fritzing 0.7.12b)
breadboards: 1

parts:
  J1 = female pin header, 14 pins [form="♀ (female)"]
  Teensy3 = female pin header, 14 pins [form="♀ (female)"]
  AnalogA = Audio Jack (TRS) 3.5mm [part_number=AnalogA package="4Ucon 08780 [THT]"]
  AnalogB = Audio Jack (TRS) 3.5mm [part_number=AnalogB package="4Ucon 08780 [THT]"]
  ThresholdA = Rotary Potentiometer (Small) [maximum_resistance=100kΩ part_number=potA]
  ThresholdB = Rotary Potentiometer (Small) [maximum_resistance=100kΩ part_number=potB]
  DetectA = LED - 5mm [color="Red (633nm)" part_number=LEDA package="5 mm [THT]"]
  DetectB = LED - 5mm [color="Red (633nm)" part_number=LEDB package="5 mm [THT]"]
  r220 = Resistor [tolerance=±5% resistance=220 package=THT]
  r220_2 = Resistor [tolerance=±5% resistance=220 package=THT]
  pot10K = female pin header, 1 pin [form="♀ (female)" part_number=PotLegA]  # not connected
  pot10k = female pin header, 1 pin [form="♀ (female)" part_number=PotLegB]  # not connected
  RF_(bottom) = female pin header, 4 pins [form="♀ (female)"]
  r140 = female pin header, 9 pins [form="♀ (female)"]
  J2 = double row male pin header, 16 pins [form="♂ (male)"]
  Buttons = double row male pin header, 16 pins [form="♂ (male)"]
  J3 = female pin header, 2 pins [form="♀ (female)"]

nets:
  N1: J1.pin1, AnalogA.Sleeve, AnalogB.Sleeve, ThresholdA.leg1, ThresholdB.leg1, DetectA.cathode, DetectB.cathode, RF_(bottom).pin2, r140.pin1, Buttons.pin1, Buttons.pin2, Buttons.pin3, Buttons.pin4, Buttons.pin5, Buttons.pin6, Buttons.pin7, Buttons.pin8, J3.pin2
  N2: J1.pin2, RF_(bottom).pin3
  N3: J1.pin3, RF_(bottom).pin4
  N4: J1.pin4, Buttons.pin16
  N5: J1.pin5, Buttons.pin15
  N6: J1.pin6, Buttons.pin14
  N7: J1.pin7, Buttons.pin13
  N8: J1.pin8, Buttons.pin12
  N9: J1.pin9, Buttons.pin11
  N10: J1.pin10, Buttons.pin10
  N11: J1.pin11, Buttons.pin9
  N12: J1.pin12, J2.pin16
  N13: J1.pin13, J2.pin15
  N14: J1.pin14, J2.pin14
  N15: Teensy3.pin1, RF_(bottom).pin1, J3.pin1
  N16: Teensy3.pin3, AnalogA.Tip, AnalogB.Tip, ThresholdA.leg2, ThresholdB.leg2
  N17: Teensy3.pin4, J2.pin10
  N18: Teensy3.pin5, J2.pin11
  N19: Teensy3.pin6, J2.pin12
  N20: Teensy3.pin7, J2.pin13
  N21: Teensy3.pin8, r220_2.Pin_0
  N22: Teensy3.pin9, r220.Pin_0
  N23: Teensy3.pin10, ThresholdB.wiper
  N24: Teensy3.pin11, ThresholdA.wiper
  N25: Teensy3.pin12, AnalogB.Ring
  N26: Teensy3.pin13, AnalogA.Ring
  N27: Teensy3.pin14, J2.pin9
  N28: DetectA.anode, r220.Pin_1
  N29: DetectB.anode, r220_2.Pin_1
  N30: r140.pin2, J2.pin1
  N31: r140.pin3, J2.pin2
  N32: r140.pin4, J2.pin3
  N33: r140.pin5, J2.pin4
  N34: r140.pin6, J2.pin5
  N35: r140.pin7, J2.pin6
  N36: r140.pin8, J2.pin7
  N37: r140.pin9, J2.pin8

notes:
  0v
  1
  2
  3
  4
  5
  6
  7
  8
  Status
  5v
  Rx
  3v3
  A0
  A1
  A2
  A3
  A4
  A5
  Tx
  Outputs
